# Fritzing sketch mudancas-layout (saved by Fritzing 0.9.3b)
breadboards: 1

parts:
  Componente1 = Arduino Uno (Rev3)
  Componente2 = Bluetooth HC-05 Macho
  R2 = Resistor [tolerance=±5% resistance=680 package="1206 [SMD]"]
  R3 = Resistor [tolerance=±5% resistance=470 package="1206 [SMD]"]
  J2 = Basic Servo
  BAT1 = Battery Holders [package=lipo-1100mAh]
  J1 = Basic Servo
  Componente3 = Display LED de 8 dígitos basado en MAX7219  # not connected
  Componente4 = Display LED de 8 dígitos basado en MAX7219  # not connected

nets:
  N1: Componente1.D2, Componente2.TXD
  N2: Componente1.D3_PWM, R3.Pin_0
  N3: Componente1.D4, J2.pulse
  N4: Componente1.D5_PWM, J1.pulse
  5V: Componente1.5V, Componente2.VCC
  GND: Componente1.GND, Componente2.GND, R2.Pin_1, J2.gnd, BAT1.-, J1.gnd
  N5: Componente2.RXD, R2.Pin_0, R3.Pin_1
  VCC: J2.vcc, BAT1.+, J1.vcc
